// Logisim project botanical_garden_game.circ as structural Verilog: 12 circuits, main circuit main
module main (
  input  in_1
);

  wire clock, clockDisplay, display_umidita_1_out_4, display_umidita_1_out_5, display_umidita_1_out_6,
       display_umidita_1_out_7, display_umidita_1_out_8, display_umidita_1_out_9, display_umidita_1_out_10,
       display_umidita_1_out_11, display_umidita_1_out_12, display_umidita_1_out_13,
       display_umidita_1_out_14, display_umidita_1_out_15, display_umidita_1_out_16,
       display_umidita_1_out_17, display_umidita_1_out_18, display_umidita_1_out_19, displayReset, gameOver,
       not_1_out, Pota_le_piante, Pulsante_irrigazione, pulsanteReset, reset, Riempi_serbatoio;
  wire [1:0] stato_serra;
  wire [4:0] display_rubinetto_1_out_4, display_rubinetto_1_out_5, display_rubinetto_1_out_6,
       display_rubinetto_1_out_7, display_rubinetto_1_out_8, display_rubinetto_1_out_9,
       display_rubinetto_1_out_10, display_rubinetto_1_out_11, display_rubinetto_1_out_12,
       display_rubinetto_1_out_13, display_rubinetto_1_out_14, display_rubinetto_1_out_15,
       display_rubinetto_1_out_16, display_rubinetto_1_out_17, display_rubinetto_1_out_18,
       display_rubinetto_1_out_19, percentuale_1_out_2, percentuale_1_out_3, percentuale_1_out_4,
       percentuale_1_out_5, percentuale_1_out_6, rubinetto_1_out_1, rubinetto_1_out_2, rubinetto_1_out_3;
  wire [6:0] asciiC, valoreAcqua, valoreHum;
  wire [11:0] display_serbatoio_1_out_4, display_serbatoio_1_out_5, display_serbatoio_1_out_6,
       display_serbatoio_1_out_7, display_serbatoio_1_out_8, display_serbatoio_1_out_9,
       display_serbatoio_1_out_10, display_serbatoio_1_out_11, display_serbatoio_1_out_12,
       display_serbatoio_1_out_13;
  wire [15:0] punteggio;
  wire [26:0] display_piante_1_out_5, display_piante_1_out_6, display_piante_1_out_7, display_piante_1_out_8,
       display_piante_1_out_9, display_piante_1_out_10, display_piante_1_out_11, display_piante_1_out_12,
       display_piante_1_out_13, display_piante_1_out_14, display_piante_1_out_15, display_piante_1_out_16,
       display_piante_1_out_17, display_piante_1_out_18, display_piante_1_out_19, display_piante_1_out_20;

  TTY_DISPLAY_DRIVER tty_display_driver_1 (
    .punteggio(punteggio), .clock(clock), .pota(Pota_le_piante), .asciiCharacter(asciiC), .reset(reset),
    .reset_2(displayReset), .clock_2(clockDisplay));
  Button button_1 (.out(Pulsante_irrigazione));
  Button button_2 (.out(Riempi_serbatoio));
  Button button_3 (.out(Pota_le_piante));
  Button button_4 (.out(pulsanteReset));
  TTY #(.rows(1), .cols(16)) tty_1 (.data(asciiC), .clk(clockDisplay), .clr(displayReset));  // open: we
  GESTIONE_UMIDITA gestione_umidita_1 (
    .Pulsante_irrigazione(Pulsante_irrigazione), .clock(clock), .reset(reset), .\valore_umidità (valoreHum),
    .valoreAcqua(valoreAcqua), .gameOver(gameOver));
  LED led_1 (.in(in_1));
  DISPLAY_PIANTE display_piante_1 (
    .clock(clock), .out_5(display_piante_1_out_5), .out_6(display_piante_1_out_6),
    .out_7(display_piante_1_out_7), .out_8(display_piante_1_out_8), .out_9(display_piante_1_out_9),
    .out_10(display_piante_1_out_10), .out_11(display_piante_1_out_11), .out_12(display_piante_1_out_12),
    .out_13(display_piante_1_out_13), .out_14(display_piante_1_out_14), .out_15(display_piante_1_out_15),
    .out_16(display_piante_1_out_16), .out_17(display_piante_1_out_17), .out_18(display_piante_1_out_18),
    .out_19(display_piante_1_out_19), .out_20(display_piante_1_out_20), .RESET(reset), .STATO(stato_serra));  // open: out_4
  DotMatrix #(.inputtype("row"), .matrixcols(27), .matrixrows(16)) dotmatrix_1 (
    .row0(display_piante_1_out_5), .row1(display_piante_1_out_6), .row2(display_piante_1_out_7),
    .row3(display_piante_1_out_8), .row4(display_piante_1_out_9), .row5(display_piante_1_out_10),
    .row6(display_piante_1_out_11), .row7(display_piante_1_out_12), .row8(display_piante_1_out_13),
    .row9(display_piante_1_out_14), .row10(display_piante_1_out_15), .row11(display_piante_1_out_16),
    .row12(display_piante_1_out_17), .row13(display_piante_1_out_18), .row14(display_piante_1_out_19),
    .row15(display_piante_1_out_20));
  // DotMatrix #(.inputtype("select"), .matrixcols(32), .matrixrows(4)) dotmatrix_2: pin names not known
  GESTIONE_STATI gestione_stati_1 (
    .VALORE_HUM(valoreHum), .clock(clock), .reset(reset), .potare(Pota_le_piante),
    .currentPunteggio(punteggio), .currentState(stato_serra));
  DotMatrix #(.inputtype("row"), .matrixcols(12), .matrixrows(10)) dotmatrix_3 (
    .row0(display_serbatoio_1_out_4), .row1(display_serbatoio_1_out_5), .row2(display_serbatoio_1_out_6),
    .row3(display_serbatoio_1_out_7), .row4(display_serbatoio_1_out_8), .row5(display_serbatoio_1_out_9),
    .row6(display_serbatoio_1_out_10), .row7(display_serbatoio_1_out_11), .row8(display_serbatoio_1_out_12),
    .row9(display_serbatoio_1_out_13));
  DISPLAY_SERBATOIO display_serbatoio_1 (
    .\quantità_acqua (valoreAcqua), .reset(reset), .out_4(display_serbatoio_1_out_4),
    .out_5(display_serbatoio_1_out_5), .out_6(display_serbatoio_1_out_6), .out_7(display_serbatoio_1_out_7),
    .out_8(display_serbatoio_1_out_8), .out_9(display_serbatoio_1_out_9),
    .out_10(display_serbatoio_1_out_10), .out_11(display_serbatoio_1_out_11),
    .out_12(display_serbatoio_1_out_12), .out_13(display_serbatoio_1_out_13), .clock(clock));
  DotMatrix #(.inputtype("row"), .matrixrows(3)) dotmatrix_4 (
    .row0(rubinetto_1_out_1), .row1(rubinetto_1_out_2), .row2(rubinetto_1_out_3));
  RUBINETTO rubinetto_1 (.out_1(rubinetto_1_out_1), .out_2(rubinetto_1_out_2), .out_3(rubinetto_1_out_3));
  DotMatrix #(.inputtype("row"), .matrixrows(16)) dotmatrix_5 (
    .row0(display_rubinetto_1_out_19), .row1(display_rubinetto_1_out_18), .row2(display_rubinetto_1_out_17),
    .row3(display_rubinetto_1_out_16), .row4(display_rubinetto_1_out_15), .row5(display_rubinetto_1_out_14),
    .row6(display_rubinetto_1_out_13), .row7(display_rubinetto_1_out_12), .row8(display_rubinetto_1_out_11),
    .row9(display_rubinetto_1_out_10), .row10(display_rubinetto_1_out_9), .row11(display_rubinetto_1_out_8),
    .row12(display_rubinetto_1_out_7), .row13(display_rubinetto_1_out_6), .row14(display_rubinetto_1_out_5),
    .row15(display_rubinetto_1_out_4));
  DISPLAY_RUBINETTO display_rubinetto_1 (
    .out_4(display_rubinetto_1_out_4), .out_5(display_rubinetto_1_out_5), .out_6(display_rubinetto_1_out_6),
    .out_7(display_rubinetto_1_out_7), .out_8(display_rubinetto_1_out_8), .out_9(display_rubinetto_1_out_9),
    .out_10(display_rubinetto_1_out_10), .out_11(display_rubinetto_1_out_11),
    .out_12(display_rubinetto_1_out_12), .out_13(display_rubinetto_1_out_13),
    .out_14(display_rubinetto_1_out_14), .out_15(display_rubinetto_1_out_15),
    .out_16(display_rubinetto_1_out_16), .out_17(display_rubinetto_1_out_17),
    .out_18(display_rubinetto_1_out_18), .out_19(display_rubinetto_1_out_19), .CLOCK(clock),
    .PULSANTE(Pulsante_irrigazione), .valoreAcqua(valoreAcqua));
  DISPLAY_UMIDITA display_umidita_1 (
    .CLOCK(clock), .RESET(reset), .out_4(display_umidita_1_out_4), .out_5(display_umidita_1_out_5),
    .out_6(display_umidita_1_out_6), .out_7(display_umidita_1_out_7), .out_8(display_umidita_1_out_8),
    .out_9(display_umidita_1_out_9), .out_10(display_umidita_1_out_10), .out_11(display_umidita_1_out_11),
    .out_12(display_umidita_1_out_12), .out_13(display_umidita_1_out_13), .out_14(display_umidita_1_out_14),
    .out_15(display_umidita_1_out_15), .out_16(display_umidita_1_out_16), .out_17(display_umidita_1_out_17),
    .out_18(display_umidita_1_out_18), .out_19(display_umidita_1_out_19), .valoreHum(valoreHum));
  _7_Segment_Display u_7_segment_display_1 (
    .g(display_umidita_1_out_10), .f(display_umidita_1_out_9), .a(display_umidita_1_out_4),
    .b(display_umidita_1_out_5), .e(display_umidita_1_out_8), .d(display_umidita_1_out_7),
    .c(display_umidita_1_out_6), .dp(display_umidita_1_out_11));
  GESTIONE_ACQUA gestione_acqua_1 (
    .riempi_serbatoio(Riempi_serbatoio), .clock(clock), .reset(reset), .valoreAcquaAttuale(valoreAcqua),
    .pulsanteIrrigazione(Pulsante_irrigazione));
  _7_Segment_Display u_7_segment_display_2 (
    .g(display_umidita_1_out_18), .f(display_umidita_1_out_17), .a(display_umidita_1_out_12),
    .b(display_umidita_1_out_13), .e(display_umidita_1_out_16), .d(display_umidita_1_out_15),
    .c(display_umidita_1_out_14), .dp(display_umidita_1_out_19));
  DotMatrix #(.inputtype("row"), .matrixrows(5)) dotmatrix_6 (
    .row0(percentuale_1_out_6), .row1(percentuale_1_out_5), .row2(percentuale_1_out_4),
    .row3(percentuale_1_out_3), .row4(percentuale_1_out_2));
  PERCENTUALE percentuale_1 (
    .out_2(percentuale_1_out_2), .out_3(percentuale_1_out_3), .out_4(percentuale_1_out_4),
    .out_5(percentuale_1_out_5), .out_6(percentuale_1_out_6), .RESET(reset));
  Clock clock_1 (.out(clock));
  not not_1 (not_1_out, in_1);
  or or_1 (reset, pulsanteReset, not_1_out, gameOver);

  // Other names for the same wires on the sheet: ON = in_1

  // Notes on the sheet:
  //   Driver TTY Display
  //   ISTRUZIONI PER GIOCARE:
  //   Punteggio
  //   1) Avviare il gioco premendo l'apposito pulsante di accensione.
  //   2) Irrigare il terreno attraverso il pulsante di irrigazione, e tenere l'umidità nel range 50 - 70%.
  //   3) Aspettare la crescita delle piantine, e potarle per ottenere punti.
  //   4) Mantenere il serbatoio dell'acqua pieno, per evitare di rimanerne senza.
  //   Gestione umidità
  //   Gestione stati
  //   Gestione acqua
endmodule

module DISPLAY_PIANTE (
  input  [1:0] STATO,
  input  RESET,
  input  clock,
  output [3:0] out_4,
  output [26:0] out_5,
  output [26:0] out_6,
  output [26:0] out_7,
  output [26:0] out_8,
  output [26:0] out_9,
  output [26:0] out_10,
  output [26:0] out_11,
  output [26:0] out_12,
  output [26:0] out_13,
  output [26:0] out_14,
  output [26:0] out_15,
  output [26:0] out_16,
  output [26:0] out_17,
  output [26:0] out_18,
  output [26:0] out_19,
  output [26:0] out_20
);

  wire [26:0] riga1, riga2, riga3, riga4, riga5, riga6, riga7, riga8, riga9, riga10, riga11, riga12, riga13,
       riga14, riga15, riga16;

  Multiplexer #(.select(2), .width(27), .enable("false")) multiplexer_1 (
    .in0({27{1'b0}}), .in1({27{1'b0}}), .in2({27{1'b0}}), .in3({27{1'b0}}), .out(riga1), .sel(STATO));
  Multiplexer #(.select(2), .width(27), .enable("false")) multiplexer_2 (
    .in0({27{1'b0}}), .in1({27{1'b0}}), .in2({27{1'b0}}), .in3({27{1'b0}}), .out(riga2), .sel(STATO));
  Multiplexer #(.select(2), .width(27), .enable("false")) multiplexer_3 (
    .in0({27{1'b0}}), .in1({27{1'b0}}), .in2({27{1'b0}}), .in3(27'h842108), .out(riga3), .sel(STATO));
  Multiplexer #(.select(2), .width(27), .enable("false")) multiplexer_4 (
    .in0({27{1'b0}}), .in1({27{1'b0}}), .in2({27{1'b0}}), .in3(27'h842108), .out(riga4), .sel(STATO));
  Multiplexer #(.select(2), .width(27), .enable("false")) multiplexer_5 (
    .in0({27{1'b0}}), .in1({27{1'b0}}), .in2({27{1'b0}}), .in3(27'h1ce739c), .out(riga5), .sel(STATO));
  Multiplexer #(.select(2), .width(27), .enable("false")) multiplexer_6 (
    .in0({27{1'b0}}), .in1({27{1'b0}}), .in2(27'h842108), .in3(27'h842108), .out(riga6), .sel(STATO));
  Multiplexer #(.select(2), .width(27), .enable("false")) multiplexer_7 (
    .in0({27{1'b0}}), .in1({27{1'b0}}), .in2(27'h842108), .in3(27'h842108), .out(riga7), .sel(STATO));
  Multiplexer #(.select(2), .width(27), .enable("false")) multiplexer_8 (
    .in0({27{1'b0}}), .in1({27{1'b0}}), .in2(27'h1ce739c), .in3(27'h1ce739c), .out(riga8), .sel(STATO));
  Multiplexer #(.select(2), .width(27), .enable("false")) multiplexer_9 (
    .in0({27{1'b0}}), .in1(27'h842108), .in2(27'h842108), .in3(27'h842108), .out(riga9), .sel(STATO));
  Multiplexer #(.select(2), .width(27), .enable("false")) multiplexer_10 (
    .in0({27{1'b0}}), .in1(27'h842108), .in2(27'h842108), .in3(27'h842108), .out(riga10), .sel(STATO));
  Multiplexer #(.select(2), .width(27), .enable("false")) multiplexer_11 (
    .in0({27{1'b0}}), .in1(27'h1ce739c), .in2(27'h1ce739c), .in3(27'h1ce739c), .out(riga11), .sel(STATO));
  Multiplexer #(.select(2), .width(27), .enable("false")) multiplexer_12 (
    .in0({27{1'b0}}), .in1(27'h842108), .in2(27'h842108), .in3(27'h842108), .out(riga12), .sel(STATO));
  Multiplexer #(.select(2), .width(27), .enable("false")) multiplexer_13 (
    .in0({27{1'b0}}), .in1(27'h842108), .in2(27'h842108), .in3(27'h842108), .out(riga13), .sel(STATO));
  Multiplexer #(.select(2), .width(27), .enable("false")) multiplexer_14 (
    .in0({27{1'b0}}), .in1(27'h1ce739c), .in2(27'h1ce739c), .in3(27'h1ce739c), .out(riga14), .sel(STATO));
  Multiplexer #(.select(2), .width(27), .enable("false")) multiplexer_15 (
    .in0(27'h842108), .in1(27'h842108), .in2(27'h842108), .in3(27'h842108), .out(riga15), .sel(STATO));
  Multiplexer #(.select(2), .width(27), .enable("false")) multiplexer_16 (
    .in0(27'h842108), .in1(27'h842108), .in2(27'h842108), .in3(27'h842108), .out(riga16), .sel(STATO));
  Register #(.width(27)) register_1 (.D(riga1), .Q(out_5), .clk(clock), .clr(RESET));  // open: en
  Register #(.width(27)) register_2 (.D(riga2), .Q(out_6), .clk(clock), .clr(RESET));  // open: en
  Register #(.width(27)) register_3 (.D(riga3), .Q(out_7), .clk(clock), .clr(RESET));  // open: en
  Register #(.width(27)) register_4 (.D(riga4), .Q(out_8), .clk(clock), .clr(RESET));  // open: en
  Register #(.width(27)) register_5 (.D(riga5), .Q(out_9), .clk(clock), .clr(RESET));  // open: en
  Register #(.width(27)) register_6 (.D(riga6), .Q(out_10), .clk(clock), .clr(RESET));  // open: en
  Register #(.width(27)) register_7 (.D(riga7), .Q(out_11), .clk(clock), .clr(RESET));  // open: en
  Register #(.width(27)) register_8 (.D(riga8), .Q(out_12), .clk(clock), .clr(RESET));  // open: en
  Register #(.width(27)) register_9 (.D(riga9), .Q(out_13), .clk(clock), .clr(RESET));  // open: en
  Register #(.width(27)) register_10 (.D(riga10), .Q(out_14), .clk(clock), .clr(RESET));  // open: en
  Register #(.width(27)) register_11 (.D(riga11), .Q(out_15), .clk(clock), .clr(RESET));  // open: en
  Register #(.width(27)) register_12 (.D(riga12), .Q(out_16), .clk(clock), .clr(RESET));  // open: en
  Register #(.width(27)) register_13 (.D(riga13), .Q(out_17), .clk(clock), .clr(RESET));  // open: en
  Register #(.width(27)) register_14 (.D(riga14), .Q(out_18), .clk(clock), .clr(RESET));  // open: en
  Register #(.width(27)) register_15 (.D(riga15), .Q(out_19), .clk(clock), .clr(RESET));  // open: en
  Register #(.width(27)) register_16 (.D(riga16), .Q(out_20), .clk(clock), .clr(RESET));  // open: en

  assign out_4 = 4'b0000;

  // Other names for the same wires on the sheet: clear = RESET

  // Notes on the sheet:
  //   uscita aggiuntiva per sistemare il colore del terreno
endmodule

module DISPLAY_RUBINETTO (
  input  CLOCK,
  input  PULSANTE,
  input  [6:0] valoreAcqua,
  output [4:0] out_4,
  output [4:0] out_5,
  output [4:0] out_6,
  output [4:0] out_7,
  output [4:0] out_8,
  output [4:0] out_9,
  output [4:0] out_10,
  output [4:0] out_11,
  output [4:0] out_12,
  output [4:0] out_13,
  output [4:0] out_14,
  output [4:0] out_15,
  output [4:0] out_16,
  output [4:0] out_17,
  output [4:0] out_18,
  output [4:0] out_19
);

  wire and_1_out, comparator_1_gt;
  wire [4:0] multiplexer_1_out;

  Comparator #(.width(7), .mode("unsigned")) comparator_1 (
    .a(valoreAcqua), .b({7{1'b0}}), .gt(comparator_1_gt));  // open: eq, lt
  and and_1 (and_1_out, comparator_1_gt, PULSANTE);
  Multiplexer #(.width(5), .enable("false")) multiplexer_1 (
    .in0({5{1'b0}}), .in1(5'b00100), .out(multiplexer_1_out), .sel(and_1_out));
  Register #(.width(5)) register_1 (.D(out_5), .Q(out_4), .clk(CLOCK));  // open: en, clr
  Register #(.width(5)) register_2 (.D(out_6), .Q(out_5), .clk(CLOCK));  // open: en, clr
  Register #(.width(5)) register_3 (.D(out_7), .Q(out_6), .clk(CLOCK));  // open: en, clr
  Register #(.width(5)) register_4 (.D(out_8), .Q(out_7), .clk(CLOCK));  // open: en, clr
  Register #(.width(5)) register_5 (.D(out_9), .Q(out_8), .clk(CLOCK));  // open: en, clr
  Register #(.width(5)) register_6 (.D(out_10), .Q(out_9), .clk(CLOCK));  // open: en, clr
  Register #(.width(5)) register_7 (.D(out_11), .Q(out_10), .clk(CLOCK));  // open: en, clr
  Register #(.width(5)) register_8 (.D(out_12), .Q(out_11), .clk(CLOCK));  // open: en, clr
  Register #(.width(5)) register_9 (.D(out_13), .Q(out_12), .clk(CLOCK));  // open: en, clr
  Register #(.width(5)) register_10 (.D(out_14), .Q(out_13), .clk(CLOCK));  // open: en, clr
  Register #(.width(5)) register_11 (.D(out_15), .Q(out_14), .clk(CLOCK));  // open: en, clr
  Register #(.width(5)) register_12 (.D(out_16), .Q(out_15), .clk(CLOCK));  // open: en, clr
  Register #(.width(5)) register_13 (.D(out_17), .Q(out_16), .clk(CLOCK));  // open: en, clr
  Register #(.width(5)) register_14 (.D(out_18), .Q(out_17), .clk(CLOCK));  // open: en, clr
  Register #(.width(5)) register_15 (.D(out_19), .Q(out_18), .clk(CLOCK));  // open: en, clr
  Register #(.width(5)) register_16 (.D(multiplexer_1_out), .Q(out_19), .clk(CLOCK));  // open: en, clr
endmodule

module _7_SEGMENT_DRIVER (
  input  [3:0] in_1,
  input  CLOCK,
  input  reset,
  output E,
  output G,
  output C,
  output H,
  output B,
  output D,
  output F,
  output A
);

  wire and_2_out, and_3_out, and_4_out, and_5_out, and_7_out, and_9_out, and_10_out, and_11_out, and_12_out,
       and_14_out, and_15_out, and_16_out, and_18_out, and_19_out, and_20_out, and_22_out, and_23_out,
       and_24_out, not_2_out, not_3_out, not_4_out, not_5_out, not_6_out, not_7_out, not_8_out, not_9_out,
       not_10_out, not_11_out, not_12_out, not_13_out, not_14_out, not_15_out, not_16_out, not_17_out,
       not_18_out, not_19_out, not_20_out, not_21_out, not_22_out, not_23_out, or_1_out, or_2_out, or_3_out,
       or_4_out, or_5_out, or_6_out, or_7_out, R;
  wire [3:0] register_1_q;

  Register #(.width(4)) register_1 (.D(in_1), .Q(register_1_q), .clk(CLOCK));  // open: en, clr
  not not_1 (R, reset);
  or or_1 (or_1_out, register_1_q[3], register_1_q[1], and_2_out, and_3_out);
  and and_1 (A, R, or_1_out);
  not not_2 (not_2_out, register_1_q[0]);
  not not_3 (not_3_out, register_1_q[1]);
  not not_4 (not_4_out, register_1_q[2]);
  and and_2 (and_2_out, register_1_q[2], register_1_q[0]);
  and and_3 (and_3_out, not_4_out, not_3_out, not_2_out);
  not not_5 (not_5_out, register_1_q[0]);
  not not_6 (not_6_out, register_1_q[1]);
  and and_4 (and_4_out, not_6_out, not_5_out);
  and and_5 (and_5_out, register_1_q[1], register_1_q[0]);
  not not_7 (not_7_out, register_1_q[2]);
  or or_2 (or_2_out, and_4_out, not_7_out, and_5_out, register_1_q[3]);
  and and_6 (B, R, or_2_out);
  and and_7 (and_7_out, register_1_q[2], register_1_q[1]);
  not not_8 (not_8_out, register_1_q[1]);
  and and_8 (C, R, or_3_out);
  and and_9 (and_9_out, register_1_q[1], register_1_q[0]);
  or or_3 (or_3_out, not_8_out, and_7_out, and_9_out, register_1_q[3]);
  not not_9 (not_9_out, register_1_q[1]);
  not not_10 (not_10_out, register_1_q[2]);
  not not_11 (not_11_out, register_1_q[0]);
  and and_10 (and_10_out, not_11_out, not_10_out);
  and and_11 (and_11_out, register_1_q[2], not_9_out, register_1_q[0]);
  not not_12 (not_12_out, register_1_q[2]);
  and and_12 (and_12_out, register_1_q[1], not_12_out);
  or or_4 (or_4_out, and_10_out, and_11_out, register_1_q[3], and_12_out, and_15_out);
  and and_13 (D, R, or_4_out);
  not not_13 (not_13_out, register_1_q[0]);
  not not_14 (not_14_out, register_1_q[0]);
  and and_14 (and_14_out, not_13_out, not_15_out);
  and and_15 (and_15_out, register_1_q[1], not_14_out);
  not not_15 (not_15_out, register_1_q[2]);
  not not_16 (not_16_out, register_1_q[0]);
  and and_16 (and_16_out, register_1_q[1], not_16_out);
  or or_5 (or_5_out, and_14_out, and_16_out);
  and and_17 (E, R, or_5_out);
  not not_17 (not_17_out, register_1_q[1]);
  not not_18 (not_18_out, register_1_q[0]);
  not not_19 (not_19_out, register_1_q[1]);
  and and_18 (and_18_out, not_17_out, not_18_out);
  and and_19 (and_19_out, not_19_out, register_1_q[2]);
  not not_20 (not_20_out, register_1_q[0]);
  and and_20 (and_20_out, register_1_q[1], register_1_q[2], not_20_out);
  or or_6 (or_6_out, and_18_out, and_19_out, register_1_q[3], and_20_out);
  and and_21 (F, R, or_6_out);
  not not_21 (not_21_out, register_1_q[1]);
  and and_22 (and_22_out, register_1_q[2], not_21_out);
  not not_22 (not_22_out, register_1_q[2]);
  and and_23 (and_23_out, not_22_out, register_1_q[1]);
  and and_24 (and_24_out, register_1_q[1], not_23_out);
  or or_7 (or_7_out, register_1_q[3], and_22_out, and_23_out, and_24_out);
  and and_25 (G, R, or_7_out);
  not not_23 (not_23_out, register_1_q[0]);

  assign H = 1'b0;
endmodule

module RUBINETTO (
  output [4:0] out_1,
  output [4:0] out_2,
  output [4:0] out_3
);


  assign out_1 = {5{1'b0}};
  assign out_2 = 5'b01111;
  assign out_3 = 5'b00100;
endmodule

module PERCENTUALE (
  input  RESET,
  output [4:0] out_2,
  output [4:0] out_3,
  output [4:0] out_4,
  output [4:0] out_5,
  output [4:0] out_6
);

  Multiplexer #(.width(5), .enable("false")) multiplexer_1 (.in0(5'b10001), .in1({5{1'b0}}), .out(out_2), .sel(RESET));
  Multiplexer #(.width(5), .enable("false")) multiplexer_2 (.in0(5'b00010), .in1({5{1'b0}}), .out(out_3), .sel(RESET));
  Multiplexer #(.width(5), .enable("false")) multiplexer_3 (.in0(5'b00100), .in1({5{1'b0}}), .out(out_4), .sel(RESET));
  Multiplexer #(.width(5), .enable("false")) multiplexer_4 (.in0(5'b01000), .in1({5{1'b0}}), .out(out_5), .sel(RESET));
  Multiplexer #(.width(5), .enable("false")) multiplexer_5 (.in0(5'b10001), .in1({5{1'b0}}), .out(out_6), .sel(RESET));

  // Other names for the same wires on the sheet: R1[4:0] = out_2; R2[4:0] = out_3; R3[4:0] = out_4; R4[4:0] = out_5;
  //   R5[4:0] = out_6
endmodule

module GESTIONE_STATI (
  input  [6:0] VALORE_HUM,
  input  potare,
  input  clock,
  input  reset,
  output [1:0] currentState,
  output [15:0] currentPunteggio
);

  wire and_1_out, and_2_out, comparator_2_gt, comparator_3_lt, comparator_4_eq, evolviPianta, not_1_out,
       not_2_out;
  wire [1:0] adder_1_out, bit_extender_1_out, multiplexer_2_out, multiplexer_5_out;
  wire [7:0] adder_2_out, multiplexer_1_out, multiplexer_3_out, multiplexer_4_out, Q;
  wire [15:0] adder_3_out, multiplexer_6_out, multiplexer_7_out;

  Comparator comparator_1 (.a(Q), .b(8'hc8), .eq(evolviPianta));  // open: gt, lt
  Comparator #(.width(7), .mode("unsigned")) comparator_2 (
    .a(VALORE_HUM), .b(7'b0110010), .gt(comparator_2_gt));  // open: eq, lt
  Comparator #(.width(7), .mode("unsigned")) comparator_3 (
    .a(VALORE_HUM), .b(7'b1000110), .lt(comparator_3_lt));  // open: gt, eq
  assign bit_extender_1_out = {{1{1'b0}}, not_1_out};  // Bit_Extender bit_extender_1
  not not_1 (not_1_out, comparator_4_eq);
  Comparator #(.width(2), .mode("unsigned")) comparator_4 (
    .a(2'b11), .b(currentState), .eq(comparator_4_eq));  // open: gt, lt
  not not_2 (not_2_out, evolviPianta);
  and and_1 (and_1_out, comparator_2_gt, comparator_3_lt);
  Adder #(.width(2)) adder_1 (.a(currentState), .b(bit_extender_1_out), .out(adder_1_out));  // open: cin, cout
  Multiplexer #(.width(8), .enable("false")) multiplexer_1 (
    .in0({8{1'b0}}), .in1(adder_2_out), .out(multiplexer_1_out), .sel(and_2_out));
  and and_2 (and_2_out, not_2_out, and_1_out);
  Multiplexer #(.width(2), .enable("false")) multiplexer_2 (
    .in0(currentState), .in1(adder_1_out), .out(multiplexer_2_out), .sel(evolviPianta));
  Multiplexer #(.width(8), .enable("false")) multiplexer_3 (
    .in0(multiplexer_1_out), .in1({8{1'b0}}), .out(multiplexer_3_out), .sel(potare));
  Multiplexer #(.width(8), .enable("false")) multiplexer_4 (
    .in0({8{1'b0}}), .in1(8'h1), .out(multiplexer_4_out), .sel(and_2_out));
  Multiplexer #(.width(2), .enable("false")) multiplexer_5 (
    .in0(multiplexer_2_out), .in1(2'b00), .out(multiplexer_5_out), .sel(potare));
  Register register_1 (.D(multiplexer_3_out), .Q(Q), .clk(clock), .clr(reset));  // open: en
  Adder adder_2 (.a(Q), .b(multiplexer_4_out), .out(adder_2_out));  // open: cin, cout
  Register #(.width(2)) register_2 (.D(multiplexer_5_out), .Q(currentState), .clk(clock), .clr(reset));  // open: en
  Multiplexer #(.select(2), .width(16), .enable("false")) multiplexer_6 (
    .in0({16{1'b0}}), .in1(16'ha), .in2(16'h64), .in3(16'h1f4), .out(multiplexer_6_out), .sel(currentState));
  Multiplexer #(.width(16), .enable("false")) multiplexer_7 (
    .in0({16{1'b0}}), .in1(multiplexer_6_out), .out(multiplexer_7_out), .sel(potare));
  Adder #(.width(16)) adder_3 (.a(currentPunteggio), .b(multiplexer_7_out), .out(adder_3_out));  // open: cin, cout
  Register #(.width(16)) register_3 (.D(adder_3_out), .Q(currentPunteggio), .clk(clock), .clr(reset));  // open: en

  // Other names for the same wires on the sheet: pota_le_piante = potare; valHum[6:0] = VALORE_HUM

  // Notes on the sheet:
  //   punteggi
endmodule

module GESTIONE_UMIDITA (
  input  Pulsante_irrigazione,
  input  clock,
  input  reset,
  input  [6:0] valoreAcqua,
  output gameOver,
  output [6:0] \valore_umidità 
);

  wire comparator_1_gt, comparator_3_eq, comparator_4_gt, comparator_5_lt, comparator_6_gt, d_ff_1_q,
       decrease, irriga, multiplexer_3_out, multiplexer_4_out, not_1_out, or_1_out, shift_register_1_out;
  wire [6:0] adder_1_out, adder_2_out, bit_extender_1_out, bit_extender_2_out, bit_extender_3_out,
       counter_1_q, mode, multiplexer_1_out, multiplexer_2_out, multiplexer_5_out, multiplexer_6_out,
       multiplexer_7_out, register_1_q, subtractor_1_out, subtractor_2_out;

  Counter #(.width(7), .max('h7f)) counter_1 (
    .D(counter_1_q), .Q(counter_1_q), .clk(clock), .clr(d_ff_1_q));  // open: load, count, carry
  Comparator #(.width(7), .mode("unsigned")) comparator_1 (
    .a(valoreAcqua), .b({7{1'b0}}), .gt(comparator_1_gt));  // open: eq, lt
  Comparator #(.width(7), .mode("unsigned")) comparator_2 (.a(mode), .b(counter_1_q), .eq(decrease));  // open: gt, lt
  or or_1 (or_1_out, decrease, reset);
  D_Flip_Flop d_ff_1 (.clk(clock), .D(or_1_out), .Q(d_ff_1_q));  // open: Qn, preset, en, reset
  and and_1 (irriga, comparator_1_gt, Pulsante_irrigazione);
  assign bit_extender_1_out = {{6{1'b0}}, decrease};  // Bit_Extender bit_extender_1
  Shift_Register #(.length(15)) shift_register_1 (
    .in(irriga), .clk(clock), .out(shift_register_1_out));  // open: shift, load, clr, d0, q0, d1, q1, d2, q2, d3, q3, d4, q4, d5, q5, d6, q6, d7, q7, d8, q8, d9, q9, d10, q10, d11, q11, d12, q12, d13, q13, d14, q14
  Adder #(.width(7)) adder_1 (.a(register_1_q), .b(bit_extender_1_out), .out(adder_1_out));  // open: cin, cout
  Multiplexer #(.width(7), .enable("false")) multiplexer_1 (
    .in0(adder_1_out), .in1({7{1'b0}}), .out(multiplexer_1_out), .sel(comparator_3_eq));
  Comparator #(.width(7), .mode("unsigned")) comparator_3 (
    .a(adder_1_out), .b(7'b0000010), .eq(comparator_3_eq));  // open: gt, lt
  Multiplexer #(.width(7), .enable("false")) multiplexer_2 (
    .in0({7{1'b0}}), .in1(7'b0000101), .out(multiplexer_2_out), .sel(comparator_3_eq));
  Multiplexer #(.enable("false")) multiplexer_3 (
    .in0(1'b0), .in1(decrease), .out(multiplexer_3_out), .sel(comparator_4_gt));
  Comparator #(.width(7), .mode("unsigned")) comparator_4 (
    .a(\valore_umidità ), .b({7{1'b0}}), .gt(comparator_4_gt));  // open: eq, lt
  Register #(.width(7)) register_1 (.D(multiplexer_1_out), .Q(register_1_q), .clk(clock), .clr(reset));  // open: en
  Comparator #(.width(7), .mode("unsigned")) comparator_5 (
    .a(\valore_umidità ), .b(7'b1100011), .lt(comparator_5_lt));  // open: gt, eq
  assign bit_extender_2_out = {{6{1'b0}}, multiplexer_3_out};  // Bit_Extender bit_extender_2
  Subtractor #(.width(7)) subtractor_1 (.a(mode), .b(multiplexer_2_out), .out(subtractor_1_out));  // open: bin, bout
  Comparator #(.width(7), .mode("unsigned")) comparator_6 (
    .a(subtractor_1_out), .b(7'b0000100), .gt(comparator_6_gt));  // open: eq, lt
  Multiplexer #(.enable("false")) multiplexer_4 (
    .in0(1'b0), .in1(shift_register_1_out), .out(multiplexer_4_out), .sel(comparator_5_lt));
  assign bit_extender_3_out = {{6{1'b0}}, multiplexer_4_out};  // Bit_Extender bit_extender_3
  Subtractor #(.width(7)) subtractor_2 (
    .a(adder_2_out), .b(bit_extender_2_out), .out(subtractor_2_out));  // open: bin, bout
  Register #(.width(7)) register_2 (.D(subtractor_2_out), .Q(\valore_umidità ), .clk(clock));  // open: en, clr
  Multiplexer #(.width(7), .enable("false")) multiplexer_5 (
    .in0(mode), .in1(subtractor_1_out), .out(multiplexer_5_out), .sel(comparator_6_gt));
  Adder #(.width(7)) adder_2 (.a(multiplexer_7_out), .b(bit_extender_3_out), .out(adder_2_out));  // open: cin, cout
  Multiplexer #(.width(7), .enable("false")) multiplexer_6 (
    .in0(multiplexer_5_out), .in1(7'b1100100), .out(multiplexer_6_out), .sel(reset));
  Multiplexer #(.width(7), .enable("false")) multiplexer_7 (
    .in0(7'b0110010), .in1(\valore_umidità ), .out(multiplexer_7_out), .sel(not_1_out));
  not not_1 (not_1_out, reset);
  Register #(.width(7)) register_3 (.D(multiplexer_6_out), .Q(mode), .clk(clock));  // open: en, clr
  Comparator #(.width(7)) comparator_7 (.a(\valore_umidità ), .b({7{1'b0}}), .eq(gameOver));  // open: gt, lt

  // Other names for the same wires on the sheet: valoreHum[6:0] = \valore_umidità 
endmodule

module DISPLAY_UMIDITA (
  input  [6:0] valoreHum,
  input  CLOCK,
  input  RESET,
  output out_4,
  output out_5,
  output out_6,
  output out_7,
  output out_8,
  output out_9,
  output out_10,
  output out_11,
  output out_12,
  output out_13,
  output out_14,
  output out_15,
  output out_16,
  output out_17,
  output out_18,
  output out_19
);

  wire [3:0] HUM1, HUM2;
  wire [6:0] divider_1_out, divider_1_rem;

  Divider #(.width(7)) divider_1 (
    .a(valoreHum), .b(7'b0001010), .out(divider_1_out), .rem(divider_1_rem));  // open: upper
  Bit_Extender #(.in_width(7), .out_width(4)) bit_extender_1 (.in(divider_1_out), .out(HUM1));
  Bit_Extender #(.in_width(7), .out_width(4)) bit_extender_2 (.in(divider_1_rem), .out(HUM2));
  _7_SEGMENT_DRIVER u_7_segment_driver_1 (
    .in_1(HUM1), .A(out_4), .B(out_5), .C(out_6), .D(out_7), .E(out_8), .F(out_9), .G(out_10), .H(out_11),
    .reset(RESET), .CLOCK(CLOCK));
  _7_SEGMENT_DRIVER u_7_segment_driver_2 (
    .in_1(HUM2), .A(out_12), .B(out_13), .C(out_14), .D(out_15), .E(out_16), .F(out_17), .G(out_18),
    .H(out_19), .reset(RESET), .CLOCK(CLOCK));
endmodule

module TTY_DISPLAY_DRIVER (
  input  [15:0] punteggio,
  input  pota,
  input  clock,
  input  reset,
  output clock_2,
  output reset_2,
  output [6:0] asciiCharacter
);

  wire [6:0] bit_extender_1_out, bit_extender_2_out, bit_extender_3_out, bit_extender_4_out,
       bit_extender_5_out, multiplexer_1_out, multiplexer_2_out, multiplexer_3_out, multiplexer_4_out,
       multiplexer_5_out;
  wire [15:0] adder_1_out, adder_2_out, adder_3_out, adder_4_out, adder_5_out, divider_1_out, divider_1_rem,
       divider_2_out, divider_2_rem, divider_3_out, divider_3_rem, divider_4_out, divider_4_rem;

  Divider #(.width(16)) divider_1 (.a(punteggio), .b(16'ha), .out(divider_1_out), .rem(divider_1_rem));  // open: upper
  Adder #(.width(16)) adder_1 (.a(divider_1_rem), .b(16'h30), .out(adder_1_out));  // open: cin, cout
  Divider #(.width(16)) divider_2 (
    .a(divider_1_out), .b(16'ha), .out(divider_2_out), .rem(divider_2_rem));  // open: upper
  Adder #(.width(16)) adder_2 (.a(divider_2_rem), .b(16'h30), .out(adder_2_out));  // open: cin, cout
  Bit_Extender #(.in_width(16), .out_width(7)) bit_extender_1 (.in(adder_1_out), .out(bit_extender_1_out));
  Divider #(.width(16)) divider_3 (
    .a(divider_2_out), .b(16'ha), .out(divider_3_out), .rem(divider_3_rem));  // open: upper
  Adder #(.width(16)) adder_3 (.a(divider_3_rem), .b(16'h30), .out(adder_3_out));  // open: cin, cout
  Bit_Extender #(.in_width(16), .out_width(7)) bit_extender_2 (.in(adder_2_out), .out(bit_extender_2_out));
  Divider #(.width(16)) divider_4 (
    .a(divider_3_out), .b(16'ha), .out(divider_4_out), .rem(divider_4_rem));  // open: upper
  Adder #(.width(16)) adder_4 (.a(divider_4_rem), .b(16'h30), .out(adder_4_out));  // open: cin, cout
  Bit_Extender #(.in_width(16), .out_width(7)) bit_extender_3 (.in(adder_3_out), .out(bit_extender_3_out));
  Adder #(.width(16)) adder_5 (.a(divider_4_out), .b(16'h30), .out(adder_5_out));  // open: cin, cout
  Bit_Extender #(.in_width(16), .out_width(7)) bit_extender_4 (.in(adder_4_out), .out(bit_extender_4_out));
  Bit_Extender #(.in_width(16), .out_width(7)) bit_extender_5 (.in(adder_5_out), .out(bit_extender_5_out));
  Multiplexer #(.width(7), .enable("false")) multiplexer_1 (
    .in0(bit_extender_2_out), .in1(7'b0110000), .out(multiplexer_1_out), .sel(reset));
  Multiplexer #(.width(7), .enable("false")) multiplexer_2 (
    .in0(bit_extender_1_out), .in1(7'b0110000), .out(multiplexer_2_out), .sel(reset));
  Multiplexer #(.width(7), .enable("false")) multiplexer_3 (
    .in0(bit_extender_3_out), .in1(7'b0110000), .out(multiplexer_3_out), .sel(reset));
  Multiplexer #(.width(7), .enable("false")) multiplexer_4 (
    .in0(bit_extender_4_out), .in1(7'b0110000), .out(multiplexer_4_out), .sel(reset));
  Shift_Register #(.width(7), .length(5)) shift_register_1 (
    .in({7{1'b0}}), .clk(clock), .out(asciiCharacter), .load(reset_2), .d0(multiplexer_2_out),
    .d1(multiplexer_1_out), .d2(multiplexer_3_out), .d3(multiplexer_4_out), .d4(multiplexer_5_out));  // open: shift, clr, q0, q1, q2, q3, q4
  Multiplexer #(.width(7), .enable("false")) multiplexer_5 (
    .in0(bit_extender_5_out), .in1(7'b0110000), .out(multiplexer_5_out), .sel(reset));
  or or_1 (reset_2, pota, reset);

  assign clock_2 = clock;

  // Other names for the same wires on the sheet: pota_Reset = reset_2
endmodule

module DISPLAY_SERBATOIO (
  input  clock,
  input  reset,
  input  [6:0] \quantità_acqua ,
  output [11:0] out_4,
  output [11:0] out_5,
  output [11:0] out_6,
  output [11:0] out_7,
  output [11:0] out_8,
  output [11:0] out_9,
  output [11:0] out_10,
  output [11:0] out_11,
  output [11:0] out_12,
  output [11:0] out_13
);

  wire comparator_1_gt, comparator_2_gt, comparator_3_gt, comparator_4_gt, comparator_5_gt, comparator_6_gt,
       comparator_7_gt, comparator_8_gt, comparator_9_gt, comparator_10_gt;
  wire [11:0] riga1, riga2, riga3, riga4, riga5, riga6, riga7, riga8, riga9, riga10;

  Comparator #(.width(7), .mode("unsigned")) comparator_1 (
    .a(\quantità_acqua ), .b(7'b1011001), .gt(comparator_1_gt));  // open: eq, lt
  Comparator #(.width(7), .mode("unsigned")) comparator_2 (
    .a(\quantità_acqua ), .b(7'b1001111), .gt(comparator_2_gt));  // open: eq, lt
  Comparator #(.width(7), .mode("unsigned")) comparator_3 (
    .a(\quantità_acqua ), .b(7'b1000101), .gt(comparator_3_gt));  // open: eq, lt
  Comparator #(.width(7), .mode("unsigned")) comparator_4 (
    .a(\quantità_acqua ), .b(7'b0111011), .gt(comparator_4_gt));  // open: eq, lt
  Comparator #(.width(7), .mode("unsigned")) comparator_5 (
    .a(\quantità_acqua ), .b(7'b0110001), .gt(comparator_5_gt));  // open: eq, lt
  Comparator #(.width(7), .mode("unsigned")) comparator_6 (
    .a(\quantità_acqua ), .b(7'b0100111), .gt(comparator_6_gt));  // open: eq, lt
  Comparator #(.width(7), .mode("unsigned")) comparator_7 (
    .a(\quantità_acqua ), .b(7'b0011101), .gt(comparator_7_gt));  // open: eq, lt
  Comparator #(.width(7), .mode("unsigned")) comparator_8 (
    .a(\quantità_acqua ), .b(7'b0010011), .gt(comparator_8_gt));  // open: eq, lt
  Comparator #(.width(7), .mode("unsigned")) comparator_9 (
    .a(\quantità_acqua ), .b(7'b0001001), .gt(comparator_9_gt));  // open: eq, lt
  Comparator #(.width(7), .mode("unsigned")) comparator_10 (
    .a(\quantità_acqua ), .b({7{1'b0}}), .gt(comparator_10_gt));  // open: eq, lt
  Multiplexer #(.width(12), .enable("false")) multiplexer_1 (
    .in0({12{1'b0}}), .in1({12{1'b1}}), .out(riga1), .sel(comparator_1_gt));
  Multiplexer #(.width(12), .enable("false")) multiplexer_2 (
    .in0({12{1'b0}}), .in1({12{1'b1}}), .out(riga2), .sel(comparator_2_gt));
  Multiplexer #(.width(12), .enable("false")) multiplexer_3 (
    .in0({12{1'b0}}), .in1({12{1'b1}}), .out(riga3), .sel(comparator_3_gt));
  Multiplexer #(.width(12), .enable("false")) multiplexer_4 (
    .in0({12{1'b0}}), .in1({12{1'b1}}), .out(riga4), .sel(comparator_4_gt));
  Multiplexer #(.width(12), .enable("false")) multiplexer_5 (
    .in0({12{1'b0}}), .in1({12{1'b1}}), .out(riga5), .sel(comparator_5_gt));
  Multiplexer #(.width(12), .enable("false")) multiplexer_6 (
    .in0({12{1'b0}}), .in1({12{1'b1}}), .out(riga6), .sel(comparator_6_gt));
  Multiplexer #(.width(12), .enable("false")) multiplexer_7 (
    .in0({12{1'b0}}), .in1({12{1'b1}}), .out(riga7), .sel(comparator_7_gt));
  Multiplexer #(.width(12), .enable("false")) multiplexer_8 (
    .in0({12{1'b0}}), .in1({12{1'b1}}), .out(riga8), .sel(comparator_8_gt));
  Multiplexer #(.width(12), .enable("false")) multiplexer_9 (
    .in0({12{1'b0}}), .in1({12{1'b1}}), .out(riga9), .sel(comparator_9_gt));
  Multiplexer #(.width(12), .enable("false")) multiplexer_10 (
    .in0({12{1'b0}}), .in1({12{1'b1}}), .out(riga10), .sel(comparator_10_gt));
  Register #(.width(12)) register_1 (.D(riga1), .Q(out_4), .clk(clock), .clr(reset));  // open: en
  Register #(.width(12)) register_2 (.D(riga2), .Q(out_5), .clk(clock), .clr(reset));  // open: en
  Register #(.width(12)) register_3 (.D(riga3), .Q(out_6), .clk(clock), .clr(reset));  // open: en
  Register #(.width(12)) register_4 (.D(riga4), .Q(out_7), .clk(clock), .clr(reset));  // open: en
  Register #(.width(12)) register_5 (.D(riga5), .Q(out_8), .clk(clock), .clr(reset));  // open: en
  Register #(.width(12)) register_6 (.D(riga6), .Q(out_9), .clk(clock), .clr(reset));  // open: en
  Register #(.width(12)) register_7 (.D(riga7), .Q(out_10), .clk(clock), .clr(reset));  // open: en
  Register #(.width(12)) register_8 (.D(riga8), .Q(out_11), .clk(clock), .clr(reset));  // open: en
  Register #(.width(12)) register_9 (.D(riga9), .Q(out_12), .clk(clock), .clr(reset));  // open: en
  Register #(.width(12)) register_10 (.D(riga10), .Q(out_13), .clk(clock), .clr(reset));  // open: en

  // Other names for the same wires on the sheet: clear = reset
endmodule

module GESTIONE_ACQUA (
  input  riempi_serbatoio,
  input  pulsanteIrrigazione,
  input  clock,
  input  reset,
  output [6:0] valoreAcquaAttuale
);

  wire and_1_out, and_2_out, comparator_1_lt, comparator_2_gt;
  wire [6:0] adder_1_out, bit_extender_1_out, bit_extender_2_out, multiplexer_1_out, subtractor_1_out;

  Comparator #(.width(7), .mode("unsigned")) comparator_1 (
    .a(valoreAcquaAttuale), .b(7'b1100100), .lt(comparator_1_lt));  // open: gt, eq
  and and_1 (and_1_out, riempi_serbatoio, comparator_1_lt);
  Multiplexer #(.width(7), .enable("false")) multiplexer_1 (
    .in0(adder_1_out), .in1(7'b1100100), .out(multiplexer_1_out), .sel(reset));
  Comparator #(.width(7), .mode("unsigned")) comparator_2 (
    .a(valoreAcquaAttuale), .b({7{1'b0}}), .gt(comparator_2_gt));  // open: eq, lt
  and and_2 (and_2_out, comparator_2_gt, pulsanteIrrigazione);
  assign bit_extender_1_out = {{6{1'b0}}, and_1_out};  // Bit_Extender bit_extender_1
  assign bit_extender_2_out = {{6{1'b0}}, and_2_out};  // Bit_Extender bit_extender_2
  Adder #(.width(7)) adder_1 (.a(subtractor_1_out), .b(bit_extender_1_out), .out(adder_1_out));  // open: cin, cout
  Register #(.width(7)) register_1 (.D(multiplexer_1_out), .Q(valoreAcquaAttuale), .clk(clock));  // open: en, clr
  Subtractor #(.width(7)) subtractor_1 (
    .a(valoreAcquaAttuale), .b(bit_extender_2_out), .out(subtractor_1_out));  // open: bin, bout

  // Other names for the same wires on the sheet: irriga = pulsanteIrrigazione; riempi = riempi_serbatoio;
  //   valoreAttuale[6:0] = valoreAcquaAttuale
endmodule
